# Fritzing sketch ArduinoSenderCircuitBoard (saved by Fritzing 0.7.10b)
breadboards: 1

parts:
  R1 = Resistor [tolerance=±5% resistance=22k package=THT]
  Arduino1 = Arduino
  R2 = Resistor [tolerance=±5% resistance=15k package=THT]

nets:
  N1: R1.Pin_0, Arduino1.D7
  N2: Arduino1.GND, R2.Pin_1

notes:
  black= ground, red= +12V, need on/off switch
